// Logisim project PROJETO ROBO ALISSON.circ as structural Verilog: 2 circuits, main circuit main
module main (
  input  H,
  input  L
);

  wire and_1_out, and_2_out, and_3_out, and_4_out, and_5_out, and_6_out, and_7_out, and_8_out, and_9_out,
       and_10_out, and_11_out, button_1_out, contador_1_out_3, E0, E0M, E1, E1M, not_1_out, not_2_out,
       not_3_out, not_4_out, not_5_out, not_6_out, not_7_out, not_8_out, not_9_out, not_10_out, not_11_out,
       or_1_out, or_2_out, or_3_out, or_4_out, or_5_out, or_6_out, xor_1_out;

  not not_1 (not_1_out, H);
  not not_2 (not_2_out, L);
  not not_3 (not_3_out, H);
  not not_4 (not_4_out, E0);
  not not_5 (not_5_out, L);
  not not_6 (not_6_out, L);
  not not_7 (not_7_out, E1M);
  not not_8 (not_8_out, E0M);
  and and_1 (and_1_out, not_1_out, L);
  and and_2 (and_2_out, not_2_out, E1, E0);
  and and_3 (and_3_out, not_1_out, E0, not_2_out);
  and and_4 (and_4_out, E0, not_3_out);
  and and_5 (and_5_out, not_3_out, L);
  and and_6 (and_6_out, not_3_out, not_4_out, not_5_out);
  not not_9 (not_9_out, E0M);
  and and_7 (and_7_out, not_9_out, E1M, not_10_out);
  not not_10 (not_10_out, H);
  and and_8 (and_8_out, not_6_out, E1M);
  not not_11 (not_11_out, H);
  and and_9 (and_9_out, not_11_out, E0M, not_6_out);
  and and_10 (and_10_out, E0M, E1M);
  and and_11 (and_11_out, not_7_out, not_8_out);
  or or_1 (or_1_out, and_2_out, and_3_out);
  // Probe on or_2_out
  or or_2 (or_2_out, and_4_out, and_5_out);
  // Probe on or_3_out
  or or_3 (or_3_out, H, and_6_out);
  CONTADOR contador_1 (.entrada(1'b1), .out_3(contador_1_out_3), .CK(button_1_out));  // open: out_4, out_5, out_6
  or or_4 (or_4_out, and_1_out, and_7_out);
  or or_5 (or_5_out, and_8_out, and_9_out);
  Button button_1 (.out(button_1_out));
  D_Flip_Flop d_ff_1 (.clk(contador_1_out_3), .D(and_1_out), .Q(E1));  // open: Qn, preset, en, reset
  D_Flip_Flop d_ff_2 (.clk(contador_1_out_3), .D(or_1_out), .Q(E0));  // open: Qn, preset, en, reset
  D_Flip_Flop d_ff_3 (.clk(contador_1_out_3), .D(or_4_out), .Q(E1M));  // open: Qn, preset, en, reset
  D_Flip_Flop d_ff_4 (.clk(contador_1_out_3), .D(or_5_out), .Q(E0M));  // open: Qn, preset, en, reset
  // Probe on xor_1_out
  xor xor_1 (xor_1_out, E1M, E0M);
  // Probe on or_6_out
  or or_6 (or_6_out, and_10_out, and_11_out);

  // Notes on the sheet:
  //   MEALEY
  //   MOORE
endmodule

module CONTADOR (
  input  entrada,
  input  CK,
  output out_3,
  output out_4,
  output out_5,
  output out_6
);

  wire and_1_out, and_2_out, and_3_out, and_4_out, and_5_out, and_6_out, and_7_out, and_8_out, and_9_out,
       and_10_out, and_11_out, not_1_out, not_2_out, not_3_out, not_4_out, not_5_out, or_1_out, or_2_out,
       or_3_out, or_4_out;

  not not_1 (not_1_out, entrada);
  not not_2 (not_2_out, out_3);
  not not_3 (not_3_out, out_4);
  not not_4 (not_4_out, out_5);
  not not_5 (not_5_out, out_6);
  and and_1 (and_1_out, out_3, not_1_out);
  and and_2 (and_2_out, entrada, out_4, out_5, out_6);
  and and_3 (and_3_out, entrada, not_3_out, out_5, out_6);
  and and_4 (and_4_out, out_4, not_4_out);
  and and_5 (and_5_out, out_4, not_5_out);
  and and_6 (and_6_out, out_4, not_1_out);
  and and_7 (and_7_out, out_5, not_5_out);
  and and_8 (and_8_out, out_5, not_1_out);
  and and_9 (and_9_out, entrada, not_4_out, out_6, out_6);
  and and_10 (and_10_out, entrada, not_2_out, not_5_out);
  and and_11 (and_11_out, not_1_out, out_6);
  or or_1 (or_1_out, and_1_out, and_2_out);
  or or_2 (or_2_out, and_3_out, and_4_out, and_5_out, and_6_out);
  D_Flip_Flop d_ff_1 (.clk(CK), .D(or_1_out), .Q(out_3));  // open: Qn, preset, en, reset
  D_Flip_Flop d_ff_2 (.clk(CK), .D(or_2_out), .Q(out_4));  // open: Qn, preset, en, reset
  D_Flip_Flop d_ff_3 (.clk(CK), .D(or_3_out), .Q(out_5));  // open: Qn, preset, en, reset
  or or_3 (or_3_out, and_7_out, and_8_out, and_9_out);
  D_Flip_Flop d_ff_4 (.clk(CK), .D(or_4_out), .Q(out_6));  // open: Qn, preset, en, reset
  or or_4 (or_4_out, and_10_out, and_11_out);

  // Other names for the same wires on the sheet: E0 = out_6; E1 = out_5; E2 = out_4; E3 = out_3
endmodule
